# Fritzing sketch EncuestaV2 (saved by Fritzing 0.9.3b)

parts:
  Componente1 = Arduino Uno (Rev3)
  Componente2 = Bluetooth HC-05 Macho
  S1 = Pushbutton [package="[SMD]"]
  R1 = Resistor [tolerance=±5% resistance=220 package=THT]
  S2 = Pushbutton [package="[SMD]"]
  R2 = Resistor [tolerance=±5% resistance=220 package=THT]
  S3 = Pushbutton [package="[SMD]"]
  R3 = Resistor [tolerance=±5% resistance=220 package=THT]
  S4 = Pushbutton [package="[SMD]"]
  R4 = Resistor [tolerance=±5% resistance=220 package=THT]

nets:
  GND: Componente1.GND, Componente2.GND, R1.Pin_0, R2.Pin_0, R3.Pin_0, R4.Pin_0
  N1: Componente1.D0/RX, Componente2.TXD
  N2: Componente1.D1/TX, Componente2.RXD
  N3: Componente1.D2, S1.Pin_1, S1.Pin_2, R1.Pin_1
  N4: Componente1.D3_PWM, S2.Pin_1, S2.Pin_2, R2.Pin_1
  N5: Componente1.D4, S3.Pin_1, S3.Pin_2, R3.Pin_1
  N6: Componente1.D5_PWM, S4.Pin_1, S4.Pin_2, R4.Pin_1
  5V: Componente1.5V, Componente2.VCC, S1.Pin_3, S1.Pin_4, S2.Pin_4, S3.Pin_4, S4.Pin_4
